// Logisim project CPU.circ as structural Verilog: 11 circuits, main circuit main
module main (
  input  [7:0] DIN,
  input  Cin,
  input  Run,
  input  Reset,
  output MSB,
  output LSB,
  output V,
  output Done,
  output C
);

  wire CLK_out, control_unit_1_a_in, control_unit_1_asen, control_unit_1_b_in, control_unit_1_b_out,
       control_unit_1_clear, control_unit_1_din_out, control_unit_1_ir_in, control_unit_1_r0_in,
       control_unit_1_r1_in, control_unit_1_r2_in, control_unit_1_r3_in, control_unit_1_r4_in,
       control_unit_1_r5_in, control_unit_1_r6_in, control_unit_1_r7_in;
  wire [2:0] control_unit_1_r_outs;
  wire [7:0] A__8_bit_output, arithmetic_and_logical_unit_1_g, B__8_bit_output, IR__8_bit_output,
       multiplexer_1_out, multiplexer_2_out, multiplexer_3_out, n8_bit_registers_1_r0, n8_bit_registers_1_r1,
       n8_bit_registers_1_r2, n8_bit_registers_1_r3, n8_bit_registers_1_r4, n8_bit_registers_1_r5,
       n8_bit_registers_1_r6, n8_bit_registers_1_r7;

  Clock CLK (.out(CLK_out));
  Mini_Register IR (._8_bit_Input(DIN), .in(control_unit_1_ir_in), ._8_bit_Output(IR__8_bit_output), .CLK(CLK_out));
  Multiplexer #(.select(3), .width(8), .enable("false")) multiplexer_1 (
    .in0(n8_bit_registers_1_r0), .in1(n8_bit_registers_1_r1), .in2(n8_bit_registers_1_r2),
    .in3(n8_bit_registers_1_r3), .in4(n8_bit_registers_1_r4), .in5(n8_bit_registers_1_r5),
    .in6(n8_bit_registers_1_r6), .in7(n8_bit_registers_1_r7), .out(multiplexer_1_out),
    .sel(control_unit_1_r_outs));
  Multiplexer #(.width(8), .enable("false")) multiplexer_2 (
    .in0(multiplexer_1_out), .in1(DIN), .out(multiplexer_2_out), .sel(control_unit_1_din_out));
  Multiplexer #(.width(8), .enable("false")) multiplexer_3 (
    .in0(multiplexer_2_out), .in1(B__8_bit_output), .out(multiplexer_3_out), .sel(control_unit_1_b_out));
  _8_bit_Registers u_8_bit_registers_1 (
    .Bus_D(multiplexer_3_out), .R0(n8_bit_registers_1_r0), .R1(n8_bit_registers_1_r1),
    .R2(n8_bit_registers_1_r2), .R3(n8_bit_registers_1_r3), .R4(n8_bit_registers_1_r4),
    .R5(n8_bit_registers_1_r5), .R6(n8_bit_registers_1_r6), .R7(n8_bit_registers_1_r7), .CLK(CLK_out),
    .Clear(Reset), .R0in(control_unit_1_r0_in), .R1in(control_unit_1_r1_in), .R2in(control_unit_1_r2_in),
    .R3in(control_unit_1_r3_in), .R4in(control_unit_1_r4_in), .R5in(control_unit_1_r5_in),
    .R6in(control_unit_1_r6_in), .R7in(control_unit_1_r7_in));
  Control_Unit control_unit_1 (
    .R_Outs(control_unit_1_r_outs), .Done(Done), .A_in(control_unit_1_a_in), .B_in(control_unit_1_b_in),
    .B_out(control_unit_1_b_out), .Asen(control_unit_1_asen), .DIN_out(control_unit_1_din_out),
    .IR_in(control_unit_1_ir_in), .CLEAR(control_unit_1_clear), .Cout(C), .Over_Flow(V), .RUN(Run),
    .RESET(Reset), .MSB(MSB), .LSB(LSB), .INSTRUCTION(IR__8_bit_output), .R0_in(control_unit_1_r0_in),
    .R1_in(control_unit_1_r1_in), .R2_in(control_unit_1_r2_in), .R3_in(control_unit_1_r3_in),
    .R4_in(control_unit_1_r4_in), .R5_in(control_unit_1_r5_in), .R6_in(control_unit_1_r6_in),
    .R7_in(control_unit_1_r7_in));
  _2_bit_Counter u_2_bit_counter_1 (.CLK(CLK_out), .Clear(control_unit_1_clear), .LSB(LSB), .MSB(MSB));
  // Probe on A__8_bit_output
  Mini_Register A (
    ._8_bit_Input(multiplexer_3_out), .in(control_unit_1_a_in), ._8_bit_Output(A__8_bit_output), .CLK(CLK_out));
  Arithmetic_and_Logical_Unit arithmetic_and_logical_unit_1 (
    .Cin(Cin), .Asen(control_unit_1_asen), .V(V), .C(C), .G(arithmetic_and_logical_unit_1_g),
    .A(multiplexer_3_out), .B(A__8_bit_output));  // open: s0, s1, isLogical
  Mini_Register B (
    ._8_bit_Input(arithmetic_and_logical_unit_1_g), .in(control_unit_1_b_in),
    ._8_bit_Output(B__8_bit_output), .CLK(CLK_out));
  // Probe on B__8_bit_output
endmodule

module Control_Unit (
  input  Cout,
  input  Over_Flow,
  input  RUN,
  input  RESET,
  input  MSB,
  input  LSB,
  input  [7:0] INSTRUCTION,
  output R0_in,
  output R1_in,
  output R2_in,
  output R3_in,
  output R4_in,
  output R5_in,
  output R6_in,
  output R7_in,
  output [2:0] R_Outs,
  output Done,
  output A_in,
  output B_in,
  output B_out,
  output Asen,
  output DIN_out,
  output IR_in,
  output CLEAR
);

  wire and_1_out, and_2_out, and_3_out, and_4_out, and_5_out, and_6_out, and_12_out, nor_1_out, or_1_out;
  wire [0:0] or_3_out;
  wire [7:0] multiplexer_1_out;

  and and_1 (and_1_out, LSB, ~MSB);  // AND_Gate
  and and_2 (and_2_out, ~LSB, MSB);  // AND_Gate
  and and_3 (and_3_out, LSB, MSB);
  and and_4 (and_4_out, ~LSB, MSB);  // AND_Gate
  or or_1 (or_1_out, Over_Flow, Cout);
  Multiplexer #(.width(8), .enable("false")) multiplexer_1 (
    .in0({8{1'b0}}), .in1(INSTRUCTION), .out(multiplexer_1_out), .sel(RUN));
  Demultiplexer #(.enable("false")) demultiplexer_1 (.in(or_1_out), .sel(and_4_out));  // open: out0, out1
  Multiplexer #(.select(2), .width(3), .enable("false")) multiplexer_2 (
    .in0(3'b000), .in1(multiplexer_1_out[2:0]), .in2(multiplexer_1_out[5:3]), .in3(3'b000), .out(R_Outs),
    .sel({A_in, or_3_out[0]}));
  and and_5 (and_5_out, ~multiplexer_1_out[7], and_1_out);  // AND_Gate
  and and_6 (and_6_out, multiplexer_1_out[7], ~and_1_out, and_3_out);  // AND_Gate
  and and_7 (A_in, multiplexer_1_out[7], and_1_out);
  and and_8 (B_in, multiplexer_1_out[7], and_2_out);
  and and_9 (B_out, multiplexer_1_out[7], and_3_out);
  and and_10 (Asen, multiplexer_1_out[6], multiplexer_1_out[7], and_2_out);
  and and_11 (DIN_out, multiplexer_1_out[6], ~multiplexer_1_out[7], and_1_out);  // AND_Gate
  and and_12 (and_12_out, ~multiplexer_1_out[6], ~multiplexer_1_out[7], and_1_out);  // AND_Gate
  nor nor_1 (nor_1_out, LSB, MSB);
  or or_2 (Done, and_5_out, and_6_out);
  or or_3 (or_3_out[0], B_in, and_12_out);
  Multiplexer #(.enable("false")) multiplexer_3 (.in0(1'b0), .in1(nor_1_out), .out(IR_in), .sel(RUN));
  Decoder #(.select(3)) decoder_1 (
    .out0(R0_in), .out1(R1_in), .out2(R2_in), .out3(R3_in), .out4(R4_in), .out5(R5_in), .out6(R6_in),
    .out7(R7_in), .sel(multiplexer_1_out[5:3]), .en(Done));
  or or_4 (CLEAR, Done, RESET);
endmodule

module ALU_Logic (
  input  [7:0] A,
  input  [7:0] B,
  input  s0,
  input  s1,
  output [7:0] Output
);

  wire [7:0] and_1_out, not_1_out, or_1_out, xor_1_out;

  assign xor_1_out = A ^ B;  // XOR_Gate xor_1, 8 bits wide
  assign and_1_out = A & B;  // AND_Gate and_1, 8 bits wide
  assign or_1_out = A | B;  // OR_Gate or_1, 8 bits wide
  assign not_1_out = ~A;  // NOT_Gate not_1, 8 bits wide
  Multiplexer #(.select(2), .width(8), .enable("false")) multiplexer_1 (
    .in0(and_1_out), .in1(or_1_out), .in2(xor_1_out), .in3(not_1_out), .out(Output), .sel({s0, s1}));
endmodule

// ALU
module Arithmetic_and_Logical_Unit (
  input  [7:0] A,
  input  Cin,
  input  [7:0] B,
  input  Asen,
  input  isLogical,
  input  s0,
  input  s1,
  output V,
  output C,
  output [7:0] G
);

  wire [7:0] alu_logic_1_output, multiplexer_1_out, n8_bit_adder_1_sum, negator_1_out;

  Negator negator_1 (.in(B), .out(negator_1_out));
  Multiplexer #(.width(8), .enable("false")) multiplexer_1 (
    .in0(B), .in1(negator_1_out), .out(multiplexer_1_out), .sel(Asen));
  _8_bit_Adder u_8_bit_adder_1 (
    .Sum(n8_bit_adder_1_sum), .Overflow(V), .Cout(C), .A(multiplexer_1_out), .B(A), .Cin(Cin));
  ALU_Logic alu_logic_1 (.Output(alu_logic_1_output), .A(A), .B(B), .s0(s0), .s1(s1));
  Multiplexer #(.width(8), .enable("false")) multiplexer_2 (
    .in0(n8_bit_adder_1_sum), .in1(alu_logic_1_output), .out(G), .sel(isLogical));
endmodule

module _8_bit_Adder (
  input  [7:0] A,
  input  [7:0] B,
  input  Cin,
  output [7:0] Sum,
  output Overflow,
  output Cout
);

  wire adder_1_cout, adder_2_cout, adder_3_cout, adder_4_cout, adder_5_cout, adder_6_cout, adder_7_cout;

  Adder #(.width(1)) adder_1 (.a(B[0]), .b(A[0]), .out(Sum[0]), .cin(Cin), .cout(adder_1_cout));
  Adder #(.width(1)) adder_2 (.a(B[1]), .b(A[1]), .out(Sum[1]), .cin(adder_1_cout), .cout(adder_2_cout));
  Adder #(.width(1)) adder_3 (.a(B[2]), .b(A[2]), .out(Sum[2]), .cin(adder_2_cout), .cout(adder_3_cout));
  Adder #(.width(1)) adder_4 (.a(B[3]), .b(A[3]), .out(Sum[3]), .cin(adder_3_cout), .cout(adder_4_cout));
  Adder #(.width(1)) adder_5 (.a(B[4]), .b(A[4]), .out(Sum[4]), .cin(adder_4_cout), .cout(adder_5_cout));
  Adder #(.width(1)) adder_6 (.a(B[5]), .b(A[5]), .out(Sum[5]), .cin(adder_5_cout), .cout(adder_6_cout));
  Adder #(.width(1)) adder_7 (.a(B[6]), .b(A[6]), .out(Sum[6]), .cin(adder_6_cout), .cout(adder_7_cout));
  Adder #(.width(1)) adder_8 (.a(B[7]), .b(A[7]), .out(Sum[7]), .cin(adder_7_cout), .cout(Cout));
  xor xor_1 (Overflow, adder_7_cout, Cout);
endmodule

// Registers
module _8_bit_Registers (
  input  CLK,
  input  Clear,
  input  [7:0] Bus_D,
  input  R0in,
  input  R1in,
  input  R2in,
  input  R3in,
  input  R4in,
  input  R5in,
  input  R6in,
  input  R7in,
  output [7:0] R0,
  output [7:0] R1,
  output [7:0] R2,
  output [7:0] R3,
  output [7:0] R4,
  output [7:0] R5,
  output [7:0] R6,
  output [7:0] R7
);

  wire [7:0] multiplexer_1_out, multiplexer_2_out, multiplexer_3_out, multiplexer_4_out, multiplexer_5_out,
       multiplexer_6_out, multiplexer_7_out, multiplexer_8_out;

  Multiplexer #(.width(8), .enable("false")) multiplexer_1 (
    .in1(Bus_D), .out(multiplexer_1_out), .sel(R0in));  // open: in0
  Multiplexer #(.width(8), .enable("false")) multiplexer_2 (
    .in1(Bus_D), .out(multiplexer_2_out), .sel(R1in));  // open: in0
  Multiplexer #(.width(8), .enable("false")) multiplexer_3 (
    .in1(Bus_D), .out(multiplexer_3_out), .sel(R2in));  // open: in0
  Multiplexer #(.width(8), .enable("false")) multiplexer_4 (
    .in1(Bus_D), .out(multiplexer_4_out), .sel(R3in));  // open: in0
  Multiplexer #(.width(8), .enable("false")) multiplexer_5 (
    .in1(Bus_D), .out(multiplexer_5_out), .sel(R4in));  // open: in0
  Multiplexer #(.width(8), .enable("false")) multiplexer_6 (
    .in1(Bus_D), .out(multiplexer_6_out), .sel(R5in));  // open: in0
  Multiplexer #(.width(8), .enable("false")) multiplexer_7 (
    .in1(Bus_D), .out(multiplexer_7_out), .sel(R6in));  // open: in0
  Multiplexer #(.width(8), .enable("false")) multiplexer_8 (
    .in1(Bus_D), .out(multiplexer_8_out), .sel(R7in));  // open: in0
  Register register_1 (.D(multiplexer_1_out), .Q(R0), .clk(CLK), .clr(Clear));  // open: en
  Register register_2 (.D(multiplexer_2_out), .Q(R1), .clk(CLK), .clr(Clear));  // open: en
  Register register_3 (.D(multiplexer_3_out), .Q(R2), .clk(CLK), .clr(Clear));  // open: en
  Register register_4 (.D(multiplexer_4_out), .Q(R3), .clk(CLK), .clr(Clear));  // open: en
  Register register_5 (.D(multiplexer_5_out), .Q(R4), .clk(CLK), .clr(Clear));  // open: en
  Register register_6 (.D(multiplexer_6_out), .Q(R5), .clk(CLK), .clr(Clear));  // open: en
  Register register_7 (.D(multiplexer_7_out), .Q(R6), .clk(CLK), .clr(Clear));  // open: en
  Register register_8 (.D(multiplexer_8_out), .Q(R7), .clk(CLK), .clr(Clear));  // open: en
endmodule

module Mini_Register (
  input  [7:0] _8_bit_Input,
  input  in,
  input  CLK,
  output [7:0] _8_bit_Output
);

  Register register_1 (.D(_8_bit_Input), .en(in), .Q(_8_bit_Output), .clk(CLK));  // open: clr
endmodule

module _2_bit_Counter (
  input  CLK,
  input  Clear,
  output LSB,
  output MSB
);

  wire and_1_out, and_2_out, d_ff_2_qn, not_1_out, xor_1_out;

  not not_1 (not_1_out, Clear);
  D_Flip_Flop d_ff_1 (.clk(CLK), .D(and_1_out), .Q(MSB));  // open: Qn, preset, en, reset
  and and_1 (and_1_out, not_1_out, xor_1_out);
  xor xor_1 (xor_1_out, MSB, LSB);
  D_Flip_Flop d_ff_2 (.clk(CLK), .D(and_2_out), .Q(LSB), .Qn(d_ff_2_qn));  // open: preset, en, reset
  and and_2 (and_2_out, d_ff_2_qn, not_1_out);
endmodule

module ALU (
  input  [7:0] A,
  input  [7:0] B,
  input  [4:0] G,
  input  Asen,
  output V,
  output C,
  output [7:0] G_2
);

  wire [0:0] not_1_out;
  wire [7:0] alu_logic_1_output, multiplexer_1_out, n8_bit_adder_1_sum, negator_1_out;

  Negator negator_1 (.in(B), .out(negator_1_out));
  not not_1 (not_1_out[0], Asen);
  Multiplexer #(.select(2), .width(8), .enable("false")) multiplexer_1 (
    .in0({8{1'b0}}), .in1(B), .in2(negator_1_out), .in3({8{1'b1}}), .out(multiplexer_1_out),
    .sel({Asen, not_1_out[0]}));
  _8_bit_Adder u_8_bit_adder_1 (
    .Sum(n8_bit_adder_1_sum), .Overflow(V), .Cout(C), .A(multiplexer_1_out), .B(A), .Cin(G[0]));
  ALU_Logic alu_logic_1 (.Output(alu_logic_1_output), .A(A), .B(B), .s0(G[1]), .s1(G[0]));
  Multiplexer #(.width(8), .enable("false")) multiplexer_2 (
    .in0(n8_bit_adder_1_sum), .in1(alu_logic_1_output), .out(G_2), .sel(G[3]));
endmodule

module Function_Unit (
  input  [7:0] A,
  input  [7:0] B,
  input  [4:0] G_Select,
  input  Asen,
  output Z,
  output V,
  output N,
  output C,
  output [7:0] F
);

  wire and_1_out;
  wire [6:0] alu_1_g_2;
  wire [7:0] n8_bit_shifter_1_h;

  and and_1 (and_1_out, G_Select[3], G_Select[4]);
  ALU alu_1 (.V(V), .C(C), .G_2({N, alu_1_g_2}), .A(A), .B(B), .G(G_Select), .Asen(Asen));
  _8_bit_Shifter u_8_bit_shifter_1 (.B(B), .I_R(1'b0), .H_Select(G_Select[2:0]), .H(n8_bit_shifter_1_h), .I_L(1'b0));
  Multiplexer #(.width(8), .enable("false")) multiplexer_1 (
    .in0({N, alu_1_g_2}), .in1(n8_bit_shifter_1_h), .out(F), .sel(and_1_out));
  nor nor_1 (Z, alu_1_g_2[0], alu_1_g_2[1], alu_1_g_2[2], alu_1_g_2[3], alu_1_g_2[4], alu_1_g_2[5], alu_1_g_2[6], N);
endmodule

module _8_bit_Shifter (
  input  [7:0] B,
  input  [2:0] H_Select,
  input  I_R,
  input  I_L,
  output [7:0] H
);

  wire [7:0] demultiplexer_1_out0, demultiplexer_1_out1, shifter_1_out, shifter_2_out;

  Demultiplexer #(.width(8), .enable("false")) demultiplexer_1 (
    .out0(demultiplexer_1_out0), .out1(demultiplexer_1_out1), .in(B), .sel(I_R));
  Shifter shifter_1 (.in(demultiplexer_1_out0), .\dist (H_Select), .out(shifter_1_out));
  Shifter #(.shift("lr")) shifter_2 (.in(demultiplexer_1_out1), .\dist (H_Select), .out(shifter_2_out));
  Multiplexer #(.width(8), .enable("false")) multiplexer_1 (
    .in0(shifter_1_out), .in1(shifter_2_out), .out(H), .sel(I_R));
endmodule
